# Fritzing sketch KniticV2_PCB (saved by Fritzing 0.7.12b)
breadboards: 1

parts:
  ArduinoDue = Arduino Mega
  transistorArray = ULN2803A [package=THT]
  transistorArray_2 = ULN2803A [package=THT]
  Power = male pin header, 10 pins [form="♂ (male)"]
  encoder = male pin header, 5 pins [form="♂ (male)"]
  solenoids = male pin header, 10 pins [form="♂ (male)"]
  solenoids_2 = male pin header, 8 pins [form="♂ (male)"]
  end_of_lineLeft = male pin header, 3 pins [form="♂ (male)"]
  end_of_lineRight = male pin header, 3 pins [form="♂ (male)"]
  +1 = female pin header, 1 pin [form="♀ (female)"]
  buzzer1 = female pin header, 1 pin [form="♀ (female)"]

nets:
  N1: ArduinoDue.GND, transistorArray.0V, transistorArray_2.0V, Power.pin4, encoder.pin4, end_of_lineLeft.pin2, end_of_lineRight.pin2
  N2: ArduinoDue.D9, buzzer1.pin1
  N3: ArduinoDue.D4, encoder.pin1
  N4: ArduinoDue.D3, encoder.pin2
  N5: ArduinoDue.D2, encoder.pin3
  N6: ArduinoDue.A0, end_of_lineRight.pin1
  N7: ArduinoDue.A1, end_of_lineLeft.pin3
  N8: ArduinoDue.D22, transistorArray.In_8
  N9: ArduinoDue.D23, transistorArray_2.In_1
  N10: ArduinoDue.D24, transistorArray.In_7
  N11: ArduinoDue.D25, transistorArray_2.In_2
  N12: ArduinoDue.D26, transistorArray.In_6
  N13: ArduinoDue.D27, transistorArray_2.In_3
  N14: ArduinoDue.D28, transistorArray.In_5
  N15: ArduinoDue.D29, transistorArray_2.In_4
  N16: ArduinoDue.D30, transistorArray.In_4
  N17: ArduinoDue.D31, transistorArray_2.In_5
  N18: ArduinoDue.D32, transistorArray.In_3
  N19: ArduinoDue.D33, transistorArray_2.In_6
  N20: ArduinoDue.D34, transistorArray.In_2
  N21: ArduinoDue.D35, transistorArray_2.In_7
  N22: ArduinoDue.D36, transistorArray.In_1
  N23: ArduinoDue.D37, transistorArray_2.In_8
  N24: transistorArray.COM_-_Common, transistorArray_2.COM_-_Common, Power.pin1, solenoids.pin9, solenoids.pin10
  N25: transistorArray.Out_8, solenoids_2.pin8
  N26: transistorArray.Out_7, solenoids_2.pin7
  N27: transistorArray.Out_6, solenoids_2.pin6
  N28: transistorArray.Out_5, solenoids_2.pin5
  N29: transistorArray.Out_4, solenoids_2.pin4
  N30: transistorArray.Out_3, solenoids_2.pin3
  N31: transistorArray.Out_2, solenoids_2.pin2
  N32: transistorArray.Out_1, solenoids_2.pin1
  N33: transistorArray_2.Out_8, solenoids.pin1
  N34: transistorArray_2.Out_7, solenoids.pin2
  N35: transistorArray_2.Out_6, solenoids.pin3
  N36: transistorArray_2.Out_5, solenoids.pin4
  N37: transistorArray_2.Out_4, solenoids.pin5
  N38: transistorArray_2.Out_3, solenoids.pin6
  N39: transistorArray_2.Out_2, solenoids.pin7
  N40: transistorArray_2.Out_1, solenoids.pin8
  N41: Power.pin8, encoder.pin5, end_of_lineLeft.pin1, end_of_lineRight.pin3, +1.pin1

notes:
  Knitic Version2
  16v
  5v
