# Fritzing sketch KniticV2_PCBmillingGND1Layer (saved by Fritzing 0.7.12b)
breadboards: 1

parts:
  transistorArray = ULN2803A [package=THT]
  transistorArray_2 = ULN2803A [package=THT]
  solenoids = male pin header, 10 pins [form="♂ (male)"]
  end_of_lineLeft = male pin header, 3 pins [form="♂ (male)"]
  C1 = Tantalum Capacitor [capacitance=100nF voltage=20V package="100 mil [THT, tantalum]"]
  C2 = Tantalum Capacitor [capacitance=100nF package="100 mil [THT, tantalum]"]
  C4 = Electrolytic Capacitor [capacitance=10µF voltage=50V package="100 mil [THT, electrolytic]"]
  C5 = Electrolytic Capacitor [capacitance=10µF voltage=50V package="100 mil [THT, electrolytic]"]
  ArduinoDue = Arduino Mega
  R1 = Resistor [tolerance=±5% resistance=10k package=THT]
  R2 = Resistor [tolerance=±5% resistance=10k package=THT]
  R3 = Resistor [tolerance=±5% resistance=10k package=THT]
  R4 = Resistor [tolerance=±5% resistance=10k package=THT]
  R5 = Resistor [tolerance=±5% resistance=10k package=THT]
  R6 = Resistor [tolerance=±5% resistance=10k package=THT]
  R7 = Resistor [tolerance=±5% resistance=220 package=THT]
  R8 = Resistor [tolerance=±5% resistance=220 package=THT]
  R9 = Resistor [tolerance=±5% resistance=220 package=THT]
  R10 = Resistor [tolerance=±5% resistance=220 package=THT]
  solenoids2 = male pin header, 1 pin [form="♂ (male)"]
  solenoids2_2 = male pin header, 1 pin [form="♂ (male)"]
  solenoids1 = male pin header, 1 pin [form="♂ (male)"]
  encoder = male pin header, 5 pins [form="♂ (male)"]
  solenoids_2 = male pin header, 8 pins [form="♂ (male)"]
  power1 = 52f0bd0a9f9f896d3691f0dec6d5bccd_12_hs_1.2mm_0.8mm [form="♀ (female)"]
  end_of_lineRight = male pin header, 3 pins [form="♂ (male)"]

nets:
  N1: transistorArray.In_1, ArduinoDue.D36
  N2: transistorArray.In_2, ArduinoDue.D34
  N3: transistorArray.In_3, ArduinoDue.D32
  N4: transistorArray.In_4, ArduinoDue.D30
  N5: transistorArray.In_5, ArduinoDue.D28
  N6: transistorArray.In_6, ArduinoDue.D26
  N7: transistorArray.In_7, ArduinoDue.D24
  N8: transistorArray.In_8, ArduinoDue.D22
  N9: transistorArray.0V, C1.-, C4.-, solenoids1.pin1
  N10: transistorArray.COM_-_Common, transistorArray_2.COM_-_Common, solenoids.pin9, solenoids.pin10, C1.+, C2.+, C4.+, C5.+, power1.connector0
  N11: transistorArray.Out_8, solenoids_2.pin8
  N12: transistorArray.Out_7, solenoids_2.pin7
  N13: transistorArray.Out_6, solenoids_2.pin6
  N14: transistorArray.Out_5, solenoids_2.pin5
  N15: transistorArray.Out_4, solenoids_2.pin4
  N16: transistorArray.Out_3, solenoids_2.pin3
  N17: transistorArray.Out_2, solenoids_2.pin2
  N18: transistorArray.Out_1, solenoids_2.pin1
  N19: transistorArray_2.In_1, ArduinoDue.D23
  N20: transistorArray_2.In_2, ArduinoDue.D25
  N21: transistorArray_2.In_3, ArduinoDue.D27
  N22: transistorArray_2.In_4, ArduinoDue.D29
  N23: transistorArray_2.In_5, ArduinoDue.D31
  N24: transistorArray_2.In_6, ArduinoDue.D33
  N25: transistorArray_2.In_7, ArduinoDue.D35
  N26: transistorArray_2.In_8, ArduinoDue.D37
  N27: transistorArray_2.0V, C2.-, C5.-, power1.connector1
  N28: transistorArray_2.Out_8, solenoids.pin1
  N29: transistorArray_2.Out_7, solenoids.pin2
  N30: transistorArray_2.Out_6, solenoids.pin3
  N31: transistorArray_2.Out_5, solenoids.pin4
  N32: transistorArray_2.Out_4, solenoids.pin5
  N33: transistorArray_2.Out_3, solenoids.pin6
  N34: transistorArray_2.Out_2, solenoids.pin7
  N35: transistorArray_2.Out_1, solenoids.pin8
  N36: end_of_lineLeft.pin1, R9.Pin_0
  N37: end_of_lineLeft.pin2, ArduinoDue.GND, R4.Pin_1, R5.Pin_0, R6.Pin_0, R7.Pin_1, R8.Pin_1, solenoids2.pin1, solenoids2_2.pin1, encoder.pin4, power1.connector2, end_of_lineRight.pin2
  N38: end_of_lineLeft.pin3, ArduinoDue.+5V, encoder.pin5, end_of_lineRight.pin1
  N39: ArduinoDue.D4, R1.Pin_0, R4.Pin_0
  N40: ArduinoDue.D3, R2.Pin_0, R6.Pin_1
  N41: ArduinoDue.D2, R3.Pin_0, R5.Pin_1
  N42: ArduinoDue.A0, R7.Pin_0, R9.Pin_1
  N43: ArduinoDue.A1, R8.Pin_0, R10.Pin_1
  N44: R1.Pin_1, encoder.pin1
  N45: R2.Pin_1, encoder.pin2
  N46: R3.Pin_1, encoder.pin3
  N47: R10.Pin_0, end_of_lineRight.pin3
