# Fritzing sketch KniticV201_+CompactPCB2Res (saved by Fritzing 0.8.7b)
circuit board: 8.2cm x 5.29638cm
breadboards: 1

parts:
  transistorArray = ULN2803A [package=THT]
  transistorArray_2 = ULN2803A [package=THT]
  encoder = male pin header, 5 pins [form="♂ (male)"]
  solenoids = male pin header, 10 pins [form="♂ (male)"]
  solenoids_2 = male pin header, 8 pins [form="♂ (male)"]
  end_of_lineLeft = male pin header, 3 pins [form="♂ (male)"]
  end_of_lineRight = male pin header, 3 pins [form="♂ (male)"]
  C1 = Tantalum Capacitor [capacitance=100nF voltage=20V package="100 mil [THT, tantalum]"]
  C2 = Tantalum Capacitor [capacitance=100nF package="100 mil [THT, tantalum]"]
  C4 = Electrolytic Capacitor [capacitance=10µF voltage=50V package="100 mil [THT, electrolytic]"]
  C5 = Electrolytic Capacitor [capacitance=10µF voltage=50V package="100 mil [THT, electrolytic]"]
  Buzzer = female pin header, 2 pins [form="♀ (female)"]
  power1 = Power Header [form="♀ (female)" package=THT]
  R1 = Resistor [tolerance=±5% resistance=10k package=THT]
  R2 = Resistor [tolerance=±5% resistance=10k package=THT]
  R3 = Resistor [tolerance=±5% resistance=10k package=THT]
  R4 = Resistor [tolerance=±5% resistance=10k package=THT]
  R5 = Resistor [tolerance=±5% resistance=10k package=THT]
  R6 = Resistor [tolerance=±5% resistance=10k package=THT]
  R7 = Resistor [tolerance=±5% resistance=220 package=THT]
  R8 = Resistor [tolerance=±5% resistance=220 package=THT]
  R9 = Resistor [tolerance=±5% resistance=220 package=THT]
  R10 = Resistor [tolerance=±5% resistance=220 package=THT]
  ArduinoDue = Arduino Mega 2560 (Rev3)
  16V-_-Vin = male pin header, 3 pins [form="♂ (male)"]
  Power_plug1 = Power plug  # not connected

nets:
  N1: transistorArray.In_1, ArduinoDue.D36
  N2: transistorArray.In_2, ArduinoDue.D34
  N3: transistorArray.In_3, ArduinoDue.D32
  N4: transistorArray.In_4, ArduinoDue.D30
  N5: transistorArray.In_5, ArduinoDue.D28
  N6: transistorArray.In_6, ArduinoDue.D26
  N7: transistorArray.In_7, ArduinoDue.D24
  N8: transistorArray.In_8, ArduinoDue.D22
  N9: transistorArray.COM_-_Common, transistorArray_2.COM_-_Common, solenoids.pin9, solenoids.pin10, C1.+, C2.+, C4.+, C5.+, 16V-_-Vin.pin2
  N10: transistorArray.Out_8, solenoids_2.pin8
  N11: transistorArray.Out_7, solenoids_2.pin7
  N12: transistorArray.Out_6, solenoids_2.pin6
  N13: transistorArray.Out_5, solenoids_2.pin5
  N14: transistorArray.Out_4, solenoids_2.pin4
  N15: transistorArray.Out_3, solenoids_2.pin3
  N16: transistorArray.Out_2, solenoids_2.pin2
  N17: transistorArray.Out_1, solenoids_2.pin1
  N18: transistorArray_2.In_1, ArduinoDue.D23
  N19: transistorArray_2.In_2, ArduinoDue.D25
  N20: transistorArray_2.In_3, ArduinoDue.D27
  N21: transistorArray_2.In_4, ArduinoDue.D29
  N22: transistorArray_2.In_5, ArduinoDue.D31
  N23: transistorArray_2.In_6, ArduinoDue.D33
  N24: transistorArray_2.In_7, ArduinoDue.D35
  N25: transistorArray_2.In_8, ArduinoDue.D37
  N26: transistorArray_2.Out_8, solenoids.pin1
  N27: transistorArray_2.Out_7, solenoids.pin2
  N28: transistorArray_2.Out_6, solenoids.pin3
  N29: transistorArray_2.Out_5, solenoids.pin4
  N30: transistorArray_2.Out_4, solenoids.pin5
  N31: transistorArray_2.Out_3, solenoids.pin6
  N32: transistorArray_2.Out_2, solenoids.pin7
  N33: transistorArray_2.Out_1, solenoids.pin8
  N34: encoder.pin1, R1.Pin_1
  N35: encoder.pin2, R2.Pin_1
  N36: encoder.pin3, R3.Pin_1
  N37: encoder.pin5, end_of_lineLeft.pin1, end_of_lineRight.pin3, ArduinoDue.3V3
  N38: end_of_lineLeft.pin3, R7.Pin_1
  N39: end_of_lineRight.pin1, R8.Pin_1
  N40: Buzzer.pin2, ArduinoDue.D9_PWM
  N41: power1.pin1, 16V-_-Vin.pin1
  N42: R1.Pin_0, R6.Pin_1, ArduinoDue.D4_PWM
  N43: R2.Pin_0, R5.Pin_1, ArduinoDue.D3_PWM
  N44: R3.Pin_0, R4.Pin_1, ArduinoDue.D2_PWM
  N45: R7.Pin_0, R9.Pin_1, ArduinoDue.A1
  N46: R8.Pin_0, R10.Pin_1, ArduinoDue.A0
  N47: ArduinoDue.VIN, 16V-_-Vin.pin3

notes:
  Knitic Version2.01
  16v
  5v
  GND

custom parts:
  Power Header: Knitic - header for power supply
