# Fritzing sketch KniticV1_pcb (saved by Fritzing 0.7.12b)
breadboards: 1

parts:
  ShiftOut = 74HC595 [package="DIP16 [THT]"]
  ShiftOut_2 = 74HC595 [package="DIP16 [THT]"]
  + = female pin header, 10 pins [form="♀ (female)"]
  en = male pin header, 5 pins [form="♂ (male)"]
  SensorR = male pin header, 3 pins [form="♂ (male)"]
  SensorL = male pin header, 3 pins [form="♂ (male)"]
  Solenoids = female pin header, 8 pins [form="♀ (female)"]
  C3 = Tantalum Capacitor [capacitance="1 μF" package="100 mil [THT, tantalum]"]
  TransistorArray = ULN2803A [package=THT]
  TransistorArray_2 = ULN2803A [package=THT]
  Arduino = Arduino
  buzzer = female pin header, 1 pin [form="♀ (female)"]
  +_2 = female pin header, 1 pin [form="♀ (female)"]
  V = male pin header, 10 pins [form="♂ (male)"]

nets:
  N1: ShiftOut.Q1, TransistorArray.In_7
  N2: ShiftOut.Q2, TransistorArray.In_6
  N3: ShiftOut.Q3, TransistorArray.In_5
  N4: ShiftOut.Q4, TransistorArray.In_4
  N5: ShiftOut.Q5, TransistorArray.In_3
  N6: ShiftOut.Q6, TransistorArray.In_2
  N7: ShiftOut.Q7, TransistorArray.In_1
  GND: ShiftOut.GND, ShiftOut.OE, ShiftOut_2.GND, ShiftOut_2.OE, en.pin4, SensorR.pin2, SensorL.pin2, C3.-, TransistorArray.0V, TransistorArray_2.0V, Arduino.GND, V.pin5, V.pin6, V.pin7
  N8: ShiftOut.Q7', ShiftOut_2.DS
  VCC: ShiftOut.MR, ShiftOut.VCC, ShiftOut_2.MR, ShiftOut_2.VCC, en.pin5, SensorR.pin3, SensorL.pin3, Arduino.+5V, +_2.pin1, V.pin3
  N9: ShiftOut.ST_CP, ShiftOut_2.ST_CP, C3.+, Arduino.D8
  N10: ShiftOut.DS, Arduino.D11
  N11: ShiftOut.Q0, TransistorArray.In_8
  N12: ShiftOut_2.Q1, TransistorArray_2.In_7
  N13: ShiftOut_2.Q2, TransistorArray_2.In_6
  N14: ShiftOut_2.Q3, TransistorArray_2.In_5
  N15: ShiftOut_2.Q4, TransistorArray_2.In_4
  N16: ShiftOut_2.Q5, TransistorArray_2.In_3
  N17: ShiftOut_2.Q6, TransistorArray_2.In_2
  N18: ShiftOut_2.Q7, TransistorArray_2.In_1
  N19: ShiftOut_2.SH_CP, Arduino.D12
  N20: ShiftOut_2.Q0, TransistorArray_2.In_8
  N21: +.pin1, +.pin2, TransistorArray.COM_-_Common, TransistorArray_2.COM_-_Common, V.pin10
  N22: +.pin3, TransistorArray.Out_1
  N23: +.pin4, TransistorArray.Out_2
  N24: +.pin5, TransistorArray.Out_3
  N25: +.pin6, TransistorArray.Out_4
  N26: +.pin7, TransistorArray.Out_5
  N27: +.pin8, TransistorArray.Out_6
  N28: +.pin9, TransistorArray.Out_7
  N29: +.pin10, TransistorArray.Out_8
  N30: en.pin1, Arduino.D4
  N31: en.pin2, Arduino.D3
  N32: en.pin3, Arduino.D2
  N33: SensorR.pin1, Arduino.A0
  N34: SensorL.pin1, Arduino.A1
  N35: Solenoids.pin1, TransistorArray_2.Out_1
  N36: Solenoids.pin2, TransistorArray_2.Out_2
  N37: Solenoids.pin3, TransistorArray_2.Out_3
  N38: Solenoids.pin4, TransistorArray_2.Out_4
  N39: Solenoids.pin5, TransistorArray_2.Out_5
  N40: Solenoids.pin6, TransistorArray_2.Out_6
  N41: Solenoids.pin7, TransistorArray_2.Out_7
  N42: Solenoids.pin8, TransistorArray_2.Out_8
  N43: Arduino.D9, buzzer.pin1

notes:
  Knitic
  Version_01
  +
  signalB
  2
  8
  11
  12
  3
